# Fritzing sketch PCB (saved by Fritzing 0.9.3b)
perfboards: 1

parts:
  Arduino_Nano = Arduino Nano (Rev3.0) (ICSP)
  Left_Motor = DC Motor
  Motor_Driver = Dual VNH2SP30 Motor Driver
  Right_Motor = DC Motor
  Distance_Sensor = hc-sr04
  Line_Sensor = Infrared Proximity Sensor
  12V_Lipo_Battery = LIPO-1000mAh [package=lipo-1000]

nets:
  GND: Arduino_Nano.GND, Motor_Driver.GND#138, Distance_Sensor.GND, Line_Sensor.GND
  N1: Arduino_Nano.D2, Motor_Driver.1INa
  N2: Arduino_Nano.D3, Motor_Driver.1INb
  N3: Arduino_Nano.D4, Motor_Driver.2INb#143
  N4: Arduino_Nano.D5, Motor_Driver.2INb#142
  N5: Arduino_Nano.D9, Distance_Sensor.Trig
  N6: Arduino_Nano.D10, Motor_Driver.PWM
  N7: Arduino_Nano.D11/MOSI, Motor_Driver.2PWM
  VCC: Arduino_Nano.VIN, Motor_Driver.+5V_(IN), Distance_Sensor.VCC, Line_Sensor.Vcc
  N8: Arduino_Nano.A1, Distance_Sensor.Echo
  N9: Arduino_Nano.A0, Line_Sensor.Vout
  N10: Left_Motor.pin_1, Motor_Driver.OUT_1A
  N11: Left_Motor.pin_2, Motor_Driver.OUT_1B
  N12: Motor_Driver.OUT_2A, Right_Motor.pin_1
  N13: Motor_Driver.OUT_2B, Right_Motor.pin_2
  N14: Motor_Driver.VIN, 12V_Lipo_Battery.+
  N15: Motor_Driver.GND#151, 12V_Lipo_Battery.-
